# Fritzing sketch 0908wifi (saved by Fritzing 0.9.0b)
breadboards: 1

parts:
  부품1 = Arduino Uno (Rev3)
  J1 = Basic Servo
  S2 = Toggle Switch [package=THT]
  IC1 = IC, DIP package, 8 pins [chip_label=IC]

nets:
  N1: 부품1.A0, J1.pulse
  N2: 부품1.D8, S2.L2
  N3: 부품1.D0/RX, IC1.pin1
  N4: 부품1.D1/TX, IC1.pin8
  5V: 부품1.5V, J1.vcc, IC1.pin5, IC1.pin7
  GND: 부품1.GND, J1.gnd, S2.COM, IC1.pin4

notes:
  ESP-01 WiFi Module
