# Fritzing sketch 0912wifi_PCB (saved by Fritzing 0.9.0b)
circuit board: 8.46667cm x 5.64444cm

parts:
  Arduino_nano = Arduino Nano (Rev3.0)
  Toggle = Toggle Switch [package=THT]
  LED1 = smd LED [color="Yellow (595nm)" package="1206 [SMD]"]
  R1 = Resistor [tolerance=±5% resistance=220 package=THT]
  Servo = Basic Servo
  ESP8266 = IC, DIP package, 8 pins [chip_label=IC]
  DC = Battery

nets:
  GND: Arduino_nano.GND, Toggle.COM, LED1.cathode, Servo.gnd, ESP8266.pin4, DC.-
  N1: Arduino_nano.D2, ESP8266.pin8
  N2: Arduino_nano.D3, ESP8266.pin1
  N3: Arduino_nano.D7, Toggle.L2
  N4: Arduino_nano.D8, R1.Pin_0
  N5: Arduino_nano.VIN, DC.+
  5V: Arduino_nano.5V, Servo.vcc
  N6: Arduino_nano.A0, Servo.pulse
  N7: Arduino_nano.3V3, ESP8266.pin5, ESP8266.pin7
  N8: LED1.anode, R1.Pin_1
