# Fritzing sketch 0904switch (saved by Fritzing 0.9.0b)
breadboards: 1

parts:
  부품1 = Arduino Uno (Rev3)
  S1 = Pushbutton [package="[THT]"]
  J1 = Basic Servo

nets:
  N1: 부품1.A0, J1.pulse
  N2: 부품1.D8, S1.Pin_1, S1.Pin_2
  5V: 부품1.5V, J1.vcc
  GND: 부품1.GND, S1.Pin_3, S1.Pin_4, J1.gnd
