# Fritzing sketch wifi0912_BreadBoard (saved by Fritzing 0.9.0b)
breadboards: 1

parts:
  부품1 = Arduino Uno (Rev3)
  J1 = Basic Servo
  S2 = Toggle Switch [package=THT]
  IC1 = IC, DIP package, 8 pins [chip_label=IC]
  LED1 = LED - 5mm [color="Yellow (595nm)" package="5 mm [THT]"]
  R1 = Resistor [tolerance=±5% resistance=220 package=THT]

nets:
  N1: 부품1.A0, J1.pulse
  N2: 부품1.D8, LED1.anode
  N3: 부품1.D2, IC1.pin8
  N4: 부품1.D3_PWM, IC1.pin1
  N5: 부품1.D7, S2.L2
  5V: 부품1.5V, J1.vcc, IC1.pin5, IC1.pin7
  GND: 부품1.GND, J1.gnd, S2.COM, IC1.pin4, R1.Pin_0
  N6: LED1.cathode, R1.Pin_1

notes:
  ESP-01 WiFi Module
